# Fritzing sketch hex-reader (saved by Fritzing 0.9.10b)
breadboards: 1

parts:
  Part1 = Arduino Nano (Rev3.0)
  U1 = 74HC165 [part_number=SN74LS165 package="DIP16 [THT]"]
  U2 = 74HC165 [part_number=SN74LS165 package="DIP16 [THT]"]
  JP3 = Header 4 [package=jst-4-pth]
  JP4 = Header 4 [package=jst-4-pth]
  JP5 = Header 4 [package=jst-4-pth]
  JP6 = Header 4 [package=jst-4-pth]
  SSD1306_OLED_Display = Grove OLED 128x96

nets:
  GND: Part1.GND, U1.GND, U2.GND, U2.MR, SSD1306_OLED_Display.GND
  N1: Part1.D8, U1.Q0, U2.Q0
  N2: Part1.D9, U1.Q7'
  N3: Part1.D10, U1.Q2, U2.Q2
  N4: Part1.D11/MOSI, U1.Q1, U2.Q1
  5V: Part1.5V, U1.VCC, U2.VCC, SSD1306_OLED_Display.VCC
  N5: Part1.A5, SSD1306_OLED_Display.SCL
  N6: Part1.A4, SSD1306_OLED_Display.SDA
  N7: U1.Q3, JP4.1
  N8: U1.Q4, JP4.2
  N9: U1.Q6, JP4.4
  N10: U1.MR, U2.Q7'
  N11: U1.SH_CP, JP3.1
  N12: U1.OE, JP3.3
  N13: U1.DS, JP3.4
  N14: U2.Q3, JP5.1
  N15: U2.Q4, JP5.2
  N16: U2.Q5, JP5.3
  N17: U2.Q6, JP5.4
  N18: U2.SH_CP, JP6.1
  N19: U2.ST_CP, JP6.2
  N20: U2.OE, JP6.3
  N21: U2.DS, JP6.4

notes:
  Probes
  PISO Shift Register
  I2C

custom parts:
  74HC165: 8-bit parallel-load shift registers
